// Logisim project lab6example.circ as structural Verilog: 2 circuits, main circuit main
module main (
  input  \input 
);

  wire clock_1_out;
  wire [1:0] lab1example_1_next, register_1_q;

  lab1example lab1example_1 (.state(register_1_q), .\input (\input ), .next(lab1example_1_next));
  Clock clock_1 (.out(clock_1_out));
  Register #(.width(2)) register_1 (.D(lab1example_1_next), .Q(register_1_q), .clk(clock_1_out));  // open: en, clr
endmodule

module lab1example (
  input  [1:0] state,
  input  \input ,
  output [1:0] next
);

  wire not_1_out, not_2_out, xnor_1_out, xor_1_out;

  not not_1 (not_1_out, state[1]);
  xor xor_1 (xor_1_out, state[0], \input );
  xnor xnor_1 (xnor_1_out, state[1], \input );
  not not_2 (not_2_out, state[0]);
  and and_1 (next[1], not_1_out, xor_1_out);
  and and_2 (next[0], xnor_1_out, not_2_out);
endmodule
