// Logisim project lab6example3.circ as structural Verilog: 2 circuits, main circuit main
module main (
  input  \input 
);

  wire clock_1_out;
  wire [1:0] lab6example_1_next, register_1_q;

  lab6example lab6example_1 (.state(register_1_q), .\input (\input ), .next(lab6example_1_next));
  Clock clock_1 (.out(clock_1_out));
  Register #(.width(2)) register_1 (.D(lab6example_1_next), .Q(register_1_q), .clk(clock_1_out));  // open: en, clr
endmodule

module lab6example (
  input  [1:0] state,
  input  \input ,
  output [1:0] next
);

  wire nand_1_out, not_1_out, or_1_out, xnor_1_out;

  not not_1 (not_1_out, state[0]);
  or or_1 (or_1_out, not_1_out, \input );
  Multiplexer #(.enable("false")) multiplexer_1 (.in0(or_1_out), .in1(nand_1_out), .out(next[0]), .sel(state[1]));
  nand nand_1 (nand_1_out, state[0], \input );
  Multiplexer #(.enable("false")) multiplexer_2 (.in0(state[0]), .in1(xnor_1_out), .out(next[1]), .sel(state[1]));
  xnor xnor_1 (xnor_1_out, state[0], \input );

  // Notes on the sheet:
  //   State-transition circuit
endmodule
