// Logisim project latches-flipflops-registers.circ as structural Verilog: 1 circuit, main circuit main
module main (
  input  s_prime,
  input  r_prime,
  input  a,
  input  in_4,
  input  [7:0] in_5,
  input  in_6,
  output q,
  output q_prime,
  output out_9,
  output out_10,
  output out_11,
  output [7:0] out_12
);

  wire clock_1_out, not_1_out;

  Clock clock_1 (.out(clock_1_out));
  nand nand_1 (q, s_prime, q_prime);
  nand nand_2 (q_prime, q, r_prime);
  D_Flip_Flop d_ff_1 (.clk(clock_1_out), .D(in_4), .Q(out_10));  // open: Qn, preset, en, reset
  T_Flip_Flop t_ff_1 (.clk(clock_1_out), .T(in_4), .Q(out_11));  // open: Qn, preset, reset, en
  Register register_1 (.D(in_5), .Q(out_12), .clk(in_6));  // open: en, clr
  not not_1 (not_1_out, a);
  and and_1 (out_9, a, not_1_out);

  // Notes on the sheet:
  //   D flip flop: change value on rising edge
  //   T flip flop: toggle value on rising edge
  //   S'R' Latch
endmodule
