// Logisim project latches-flipflops-registers2.circ as structural Verilog: 1 circuit, main circuit main
module main (
  input  a,
  input  b,
  input  S_prime,
  input  R_prime,
  input  a_2,
  input  in_6,
  input  [7:0] a_3,
  output a_4,
  output a_prime,
  output b_b__prime,
  output a_b__prime,
  output q,
  output q_prime,
  output out_14,
  output q_2,
  output q_3,
  output [7:0] out_17
);

  wire and_1_out, clock_1_out, not_3_out;

  Clock clock_1 (.out(clock_1_out));
  buf buffer_1 (a_4, a);
  not not_1 (a_prime, a);
  nand nand_1 (b_b__prime, b, b);
  not not_2 (a_b__prime, and_1_out);
  and and_1 (and_1_out, b, a);
  nand nand_2 (q, S_prime, q_prime);
  nand nand_3 (q_prime, q, R_prime);
  D_Flip_Flop d_ff_1 (.clk(clock_1_out), .D(in_6), .Q(q_2));  // open: Qn, preset, en, reset
  T_Flip_Flop t_ff_1 (.clk(clock_1_out), .T(in_6), .Q(q_3));  // open: Qn, preset, reset, en
  Register register_1 (.D(a_3), .Q(out_17), .clk(clock_1_out));  // open: en, clr
  and and_2 (out_14, a_2, not_3_out);
  not not_3 (not_3_out, a_2);

  // Notes on the sheet:
  //   Combinational Logic
  //   S'R' Latch
  //   Fun physics fact:
  //   D Flip-flop
  //   Toggle flip flop
  //   Register
endmodule
