// Logisim project latches-flipflops-registers3.circ as structural Verilog: 1 circuit, main circuit main
module main (
  input  a,
  input  b,
  input  S_prime,
  input  R_prime,
  input  in_5,
  input  [7:0] in_6,
  output a_2,
  output a_prime,
  output a_b__prime,
  output a_b__prime_2,
  output q,
  output q_prime,
  output out_13,
  output out_14,
  output [7:0] out_15
);

  wire and_1_out, clock_1_out;

  Clock clock_1 (.out(clock_1_out));
  buf buffer_1 (a_2, a);
  not not_1 (a_prime, a);
  nand nand_1 (a_b__prime, a, b);
  and and_1 (and_1_out, a, b);
  not not_2 (a_b__prime_2, and_1_out);
  nand nand_2 (q, S_prime, q_prime);
  nand nand_3 (q_prime, q, R_prime);
  D_Flip_Flop d_ff_1 (.clk(clock_1_out), .D(in_5), .Q(out_13));  // open: Qn, preset, en, reset
  T_Flip_Flop t_ff_1 (.clk(clock_1_out), .T(in_5), .Q(out_14));  // open: Qn, preset, reset, en
  Register register_1 (.D(in_6), .Q(out_15), .clk(clock_1_out));  // open: en, clr

  // Notes on the sheet:
  //   Combinational Logic
  //   Sequential Logic
  //   S'R' Latch
  //   1 bit memory
  //   D (Delay) Flip flop
  //   T (Toggle) flip flop
  //   Register
endmodule
