// Logisim project minority-4-1-mux.circ as structural Verilog: 1 circuit, main circuit main
module main (
  input  z,
  input  y,
  input  x,
  output minority
);

  wire not_1_out;

  not not_1 (not_1_out, z);
  Multiplexer #(.select(2), .enable("false")) multiplexer_1 (
    .in0(1'b1), .in1(not_1_out), .in2(not_1_out), .in3(1'b0), .out(minority), .sel({x, y}));

  // Notes on the sheet:
  //   Minority ciruit using a 4-1MUX
endmodule
