// Logisim project stack.circ as structural Verilog: 2 circuits, main circuit Stack8bit
module Stack8bit (
  input  [7:0] data,
  input  active,
  input  op,
  input  reset,
  output Empty,
  output [7:0] Peek
);

  wire demultiplexer_1_out0, demultiplexer_1_out1, or_1_out, xor_1_out;
  wire [7:0] adder_1_out, multiplexer_1_out, multiplexer_2_out, multiplexer_3_out, ram_1_data, SP_q, TOS_q;

  Multiplexer #(.width(8), .enable("false")) multiplexer_1 (
    .in0(8'h1), .in1({8{1'b1}}), .out(multiplexer_1_out), .sel(op));
  Adder adder_1 (.a(SP_q), .b(multiplexer_1_out), .out(adder_1_out));  // open: cin, cout
  Register SP (.D(adder_1_out), .Q(SP_q), .clk(active), .clr(reset));  // open: en
  Demultiplexer #(.enable("false")) demultiplexer_1 (
    .out0(demultiplexer_1_out0), .out1(demultiplexer_1_out1), .in(active), .sel(op));
  Comparator comparator_1 (.a({8{1'b0}}), .b(SP_q), .eq(Empty));  // open: gt, lt
  Multiplexer #(.width(8), .enable("false")) multiplexer_2 (
    .in0(SP_q), .in1(adder_1_out), .out(multiplexer_2_out), .sel(xor_1_out));
  xor xor_1 (xor_1_out, active, op);
  or or_1 (or_1_out, demultiplexer_1_out0, demultiplexer_1_out1);
  RAM #(.bus("separate")) ram_1 (
    .addr(multiplexer_2_out), .din(data), .data(ram_1_data), .str(demultiplexer_1_out0), .clk(or_1_out),
    .clr(reset));  // open: sel, ld
  Multiplexer #(.width(8), .enable("false")) multiplexer_3 (
    .in0(data), .in1(ram_1_data), .out(multiplexer_3_out), .sel(op));
  Register TOS (.D(multiplexer_3_out), .Q(TOS_q), .clk(active), .clr(reset));  // open: en
  Multiplexer #(.width(8), .enable("false")) multiplexer_4 (.in0(TOS_q), .in1(ram_1_data), .out(Peek), .sel(op));

  // Notes on the sheet:
  //   op 0 active 0: peek top
  //   op 0 active 1: push data
  //   op 1 active 0: peek under top
  //   op 1 active 1: pop
endmodule

module Stack16bit (
  input  [15:0] data,
  input  active,
  input  op,
  input  reset,
  output Empty,
  output [15:0] Peek
);

  wire demultiplexer_1_out0, demultiplexer_1_out1, or_1_out, xor_1_out;
  wire [7:0] adder_1_out, multiplexer_1_out, multiplexer_2_out, SP_q;
  wire [15:0] multiplexer_3_out, ram_1_data, TOS_q;

  Multiplexer #(.width(8), .enable("false")) multiplexer_1 (
    .in0(8'h1), .in1({8{1'b1}}), .out(multiplexer_1_out), .sel(op));
  Adder adder_1 (.a(SP_q), .b(multiplexer_1_out), .out(adder_1_out));  // open: cin, cout
  Register SP (.D(adder_1_out), .Q(SP_q), .clk(active), .clr(reset));  // open: en
  Demultiplexer #(.enable("false")) demultiplexer_1 (
    .out0(demultiplexer_1_out0), .out1(demultiplexer_1_out1), .in(active), .sel(op));
  Comparator comparator_1 (.a({8{1'b0}}), .b(SP_q), .eq(Empty));  // open: gt, lt
  Multiplexer #(.width(8), .enable("false")) multiplexer_2 (
    .in0(SP_q), .in1(adder_1_out), .out(multiplexer_2_out), .sel(xor_1_out));
  xor xor_1 (xor_1_out, active, op);
  or or_1 (or_1_out, demultiplexer_1_out0, demultiplexer_1_out1);
  RAM #(.dataWidth(16), .bus("separate")) ram_1 (
    .addr(multiplexer_2_out), .din(data), .data(ram_1_data), .str(demultiplexer_1_out0), .clk(or_1_out),
    .clr(reset));  // open: sel, ld
  Multiplexer #(.width(16), .enable("false")) multiplexer_3 (
    .in0(data), .in1(ram_1_data), .out(multiplexer_3_out), .sel(op));
  Register #(.width(16)) TOS (.D(multiplexer_3_out), .Q(TOS_q), .clk(active), .clr(reset));  // open: en
  Multiplexer #(.width(16), .enable("false")) multiplexer_4 (.in0(TOS_q), .in1(ram_1_data), .out(Peek), .sel(op));

  // Notes on the sheet:
  //   op 0 active 0: peek top
  //   op 0 active 1: push data
  //   op 1 active 0: peek under top
  //   op 1 active 1: pop
endmodule
