// Logisim project state-transition.circ as structural Verilog: 2 circuits, main circuit main
module main (
  input  in_1
);

  wire clock_1_out;
  wire [1:0] register_1_q, state_transition_1_newstate;

  state_transition state_transition_1 (.state(register_1_q), .\input (in_1), .newState(state_transition_1_newstate));
  Clock clock_1 (.out(clock_1_out));
  Register #(.width(2)) register_1 (
    .D(state_transition_1_newstate), .Q(register_1_q), .clk(clock_1_out));  // open: en, clr
endmodule

module state_transition (
  input  [1:0] state,
  input  \input ,
  output [1:0] newState
);

  wire and_1_out, nand_1_out;

  and and_1 (and_1_out, state[0], \input );
  xor xor_1 (newState[0], state[0], \input );
  Multiplexer #(.enable("false")) multiplexer_1 (.in0(and_1_out), .in1(nand_1_out), .out(newState[1]), .sel(state[1]));
  nand nand_1 (nand_1_out, state[0], \input );

  // Notes on the sheet:
  //   State transition circuit
endmodule
