// Logisim project state-transition2.circ as structural Verilog: 3 circuits, main circuit main
module main (
  input  in_1,
  input  in_2
);

  wire clock_1_out, clock_2_out, example1_1_next, register_1_q;
  wire [1:0] example2_1_next, register_2_q;

  Clock clock_1 (.out(clock_1_out));
  Clock clock_2 (.out(clock_2_out));
  example1 example1_1 (.state(register_1_q), .\input (in_1), .next(example1_1_next));
  example2 example2_1 (.state(register_2_q), .\input (in_2), .next(example2_1_next));
  Register #(.width(1)) register_1 (.D(example1_1_next), .Q(register_1_q), .clk(clock_1_out));  // open: en, clr
  Register #(.width(2)) register_2 (.D(example2_1_next), .Q(register_2_q), .clk(clock_2_out));  // open: en, clr

  // Notes on the sheet:
  //   Example 1
  //   Example 2
endmodule

module example1 (
  input  state,
  input  \input ,
  output next
);

  xnor xnor_1 (next, state, \input );
endmodule

module example2 (
  input  [1:0] state,
  input  \input ,
  output [1:0] next
);

  wire nor_1_out, or_1_out;

  or or_1 (or_1_out, state[0], \input );
  not not_1 (next[0], \input );
  Multiplexer #(.enable("false")) multiplexer_1 (.in0(or_1_out), .in1(nor_1_out), .out(next[1]), .sel(state[1]));
  nor nor_1 (nor_1_out, state[0], \input );
endmodule
