// Logisim project state-transition3.circ as structural Verilog: 3 circuits, main circuit main
module main (
  input  in_1,
  input  in_2
);

  wire clock_1_out, clock_2_out, register_1_q, state_transition_circuit_nextstate;
  wire [1:0] example2_1_next, register_2_q;

  example1 state_transition_circuit (
    .state(register_1_q), .\input (in_1), .nextState(state_transition_circuit_nextstate));
  Clock clock_1 (.out(clock_1_out));
  example2 example2_1 (.state(register_2_q), .\input (in_2), .next(example2_1_next));
  Clock clock_2 (.out(clock_2_out));
  Register #(.width(1)) register_1 (
    .D(state_transition_circuit_nextstate), .Q(register_1_q), .clk(clock_1_out));  // open: en, clr
  Register #(.width(2)) register_2 (.D(example2_1_next), .Q(register_2_q), .clk(clock_2_out));  // open: en, clr
endmodule

module example1 (
  input  state,
  input  \input ,
  output nextState
);

  xnor xnor_1 (nextState, state, \input );
endmodule

module example2 (
  input  [1:0] state,
  input  \input ,
  output [1:0] next
);

  wire xnor_1_out, xor_1_out;

  not not_1 (next[0], state[0]);
  xor xor_1 (xor_1_out, state[0], \input );
  xnor xnor_1 (xnor_1_out, state[0], \input );
  Multiplexer #(.enable("false")) multiplexer_1 (.in0(xor_1_out), .in1(xnor_1_out), .out(next[1]), .sel(state[1]));
endmodule
