// Logisim project stupid-circuit-tricks.circ as structural Verilog: 1 circuit, main circuit main
module main (
  input  z,
  input  y,
  input  x,
  output out_4
);

  Multiplexer #(.select(3), .enable("false")) multiplexer_1 (
    .in0(1'b1), .in1(1'b1), .in2(1'b0), .in3(1'b1), .in4(1'b0), .in5(1'b0), .in6(1'b1), .in7(1'b0),
    .out(out_4), .sel({x, y, z}));
endmodule
