// Logisim project stupid-circuit-tricks3.circ as structural Verilog: 1 circuit, main circuit main
module main (
  input  z,
  input  y,
  input  x,
  output out_4
);

  wire undriven, undriven_2, undriven_3;

  Multiplexer #(.select(3), .enable("false")) multiplexer_1 (
    .in0(1'b1), .in1(1'b0), .in2(1'b1), .in3(1'b1), .in4(1'b1), .in5(1'b0), .in6(1'b1), .in7(1'b0),
    .out(out_4), .sel({x, y, z}));
  Multiplexer multiplexer_2 (.in0(undriven), .in1(undriven_2), .sel(undriven_3));  // open: out, en
endmodule
